# Fritzing sketch trabalho_sistemas (saved by Fritzing 0.9.2b)

parts:
  LDR = Photocell (LDR) [package=THT]
  LED1 = smd LED [color="Green (555nm)" package="0805 [SMD]"]  # not connected
  5V = 4 x AAA Battery Mount
  POT = Resistor [tolerance=±5% resistance=10k package="2010 [SMD]"]

nets:
  N1: LDR.pin_0, POT.Pin_1
  N2: LDR.pin_1, 5V.+
  N3: 5V.-, POT.Pin_0
